# Fritzing sketch CS695 Project (saved by Fritzing 0.9.10b)
breadboards: 1

parts:
  Part1 = Adafruit Ultimate GPS v3 [part_number="Adafruit #746"]
  Part2 = OLED Monochrome 128x64 1.3 inch [part_number=938]
  Part3 = 9-DOF Absolute Orientation IMU Fusion Breakout - BNO055
  S1 = Momentary Switch [package=ksa_sealed_tac_switch]
  BeagleBone1 = BeagleBone Black
  R1 = Resistor [tolerance=±5% power=0.25 resistance=1k package=THT]
  J1 = shrouded pin header, 10 pins [form="♂ (shrouded male)"]

nets:
  VIN: Part1.VIN, Part2.VIN, Part3.5.0V, S1.1, BeagleBone1.no_name_yet#3, J1.pin9
  GND: Part1.GND, Part2.GND, Part3.GND, BeagleBone1.no_name_yet#1, R1.Pin_0, J1.pin10
  N1: Part1.RX, BeagleBone1.no_name_yet#26
  N2: Part1.TX, BeagleBone1.no_name_yet#24
  N3: Part2.MOSI_SDA, Part3.SDA_5V, BeagleBone1.no_name_yet#19
  N4: Part2.SCLK_SCK, Part3.SCL_5V, BeagleBone1.no_name_yet#20
  N5: S1.3, BeagleBone1.no_name_yet#112, R1.Pin_1
  N6: BeagleBone1.no_name_yet#11, J1.pin7
  N7: BeagleBone1.no_name_yet#13, J1.pin8

notes:
  TX
  RX
  VIN
  GND
  Laser Rangefinder

custom parts:
  Adafruit Ultimate GPS v3: We carry a few different GPS modules here in the Adafruit shop, but none that satisfied our every desire - that's why we designed this little GPS breakout board. We believe this is the Ultimate GPS module, so we named it that. It's got everything you want and more: -165 dBm sensitivity, 10 Hz updates, 66 channels 5V friendly design and only 20mA current draw Breadboard friendly + two mounting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
  OLED Monochrome 128x64 1.3 inch: These displays are small, only about 1.3" diagonal, but very readable due to the high contrast of an OLED display. This display is made of 128x64 individual white OLED pixels, each one is turned on or off by the controller chip. Because the display makes its own light, no backlight is required. This reduces the power required to run the OLED and is why the display has such high contrast; we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
  9-DOF Absolute Orientation IMU Fusion Breakout - BNO055: A MEMS accelerometer, magnetometer and gyroscope on a single die with a high speed ARM Cortex-M0 based processor to digest all the sensor data, abstract the sensor fusion and real time requirements away, and spit out data you can use in quaternions, Euler angles or vectors.
  BeagleBone Black: BeagleBone Black rev. A5B
